// Logisim project HW4(final).circ as structural Verilog: 6 circuits, main circuit main
module main (
  input  reset,
  output [15:0] out_2,
  output [15:0] out_3,
  output [15:0] out_4,
  output [15:0] out_5,
  output [11:0] out_6
);

  wire alu_1_branchcompare, and_1_out, and_2_out, and_3_out, clock_1_out, controlunit_1_alusrc,
       controlunit_1_branch, controlunit_1_call, controlunit_1_halt, controlunit_1_jump,
       controlunit_1_memread, controlunit_1_memtoreg, controlunit_1_memwrite, controlunit_1_r_type,
       controlunit_1_regdst, controlunit_1_regwrite, controlunit_1_rtn, controlunit_1_zeroreg, not_1_out,
       not_2_out, not_3_out, or_1_out;
  wire [2:0] controlunit_1_aluopcode, multiplexer_1_out, multiplexer_2_out;
  wire [15:0] adder_1_out, adder_2_out, i_type_immediate_out_2, j_type_immediate_out_2, multiplexer_3_out,
       multiplexer_4_out, multiplexer_5_out, multiplexer_6_out, PC_q, ra_q, ram_1_data, registerfile_1_data2;

  Clock clock_1 (.out(clock_1_out));
  and and_1 (and_1_out, not_1_out, clock_1_out);
  Register #(.width(16)) PC (.D(multiplexer_4_out), .en(1'b1), .Q(PC_q), .clk(and_1_out), .clr(reset));
  Adder #(.width(16)) adder_1 (.a(16'h1), .b(PC_q), .out(adder_1_out));  // open: cin, cout
  ROM #(.addrWidth(16), .dataWidth(16)) rom_1 (.addr(PC_q), .data(out_2), .sel(1'b1));
  not not_1 (not_1_out, controlunit_1_halt);
  Multiplexer #(.width(3), .enable("false")) multiplexer_1 (
    .in1({out_2[15], out_2[5:4]}), .out(multiplexer_1_out), .sel(controlunit_1_r_type));  // open: in0
  ControlUnit controlunit_1 (
    .R_type_input(multiplexer_1_out), .opcode(out_2[3:0]), .R_type(controlunit_1_r_type),
    .ALUOpcode(controlunit_1_aluopcode), .RegWrite(controlunit_1_regwrite),
    .MemWrite(controlunit_1_memwrite), .branch(controlunit_1_branch), .RegDst(controlunit_1_regdst),
    .ALUsrc(controlunit_1_alusrc), .MemRead(controlunit_1_memread), .MemToReg(controlunit_1_memtoreg),
    .jump(controlunit_1_jump), .call(controlunit_1_call), .rtn(controlunit_1_rtn), .halt(controlunit_1_halt),
    .zeroReg(controlunit_1_zeroreg));
  not not_2 (not_2_out, controlunit_1_regdst);
  Multiplexer #(.width(3), .enable("false")) multiplexer_2 (
    .in0(out_2[8:6]), .in1(out_2[11:9]), .out(multiplexer_2_out), .sel(not_2_out));
  NegativeIncludeExtend2 j_type_immediate (.in_1(out_2[15:4]), .out_2(j_type_immediate_out_2));
  NegativeIncludeExtend i_type_immediate (.in_1({out_2[15], out_2[8:4]}), .out_2(i_type_immediate_out_2));
  RegisterFile registerfile_1 (
    .RegWrite(controlunit_1_regwrite), .Write_register(multiplexer_2_out), .Read_Register1(out_2[14:12]),
    .data(out_4), .Read_Register2(out_2[11:9]), .Data1(out_5), .Data2(registerfile_1_data2), .Reset(reset),
    .clock(and_1_out), .zeroRead2(controlunit_1_zeroreg));
  not not_3 (not_3_out, controlunit_1_jump);
  Multiplexer #(.width(16), .enable("false")) multiplexer_3 (
    .in0(registerfile_1_data2), .in1(i_type_immediate_out_2), .out(multiplexer_3_out),
    .sel(controlunit_1_alusrc));
  Multiplexer #(.width(16), .enable("false")) multiplexer_4 (
    .in0(multiplexer_6_out), .in1(ra_q), .out(multiplexer_4_out), .sel(controlunit_1_rtn));
  Multiplexer #(.width(16), .enable("false")) multiplexer_5 (
    .in0(j_type_immediate_out_2), .in1(i_type_immediate_out_2), .out(multiplexer_5_out), .sel(not_3_out));
  ALU alu_1 (
    .Input_data_1(out_5), .Input_data_2(multiplexer_3_out), .ALUop(controlunit_1_aluopcode),
    .ALU_result(out_3), .branchCompare(alu_1_branchcompare));
  and and_2 (and_2_out, controlunit_1_branch, alu_1_branchcompare);
  Adder #(.width(16)) adder_2 (.a(PC_q), .b(multiplexer_5_out), .out(adder_2_out));  // open: cin, cout
  or or_1 (or_1_out, controlunit_1_jump, controlunit_1_call, and_2_out);
  Multiplexer #(.width(16), .enable("false")) multiplexer_6 (
    .in0(adder_1_out), .in1(adder_2_out), .out(multiplexer_6_out), .sel(or_1_out));
  Register #(.width(16)) ra (.D(adder_1_out), .Q(ra_q), .clk(and_3_out));  // open: en, clr
  and and_3 (and_3_out, controlunit_1_call, and_1_out);
  RAM #(.addrWidth(16), .dataWidth(16), .bus("separate")) ram_1 (
    .addr(out_5), .din(registerfile_1_data2), .data(ram_1_data), .str(controlunit_1_memwrite),
    .clk(and_1_out), .ld(controlunit_1_memread), .clr(reset));  // open: sel
  Multiplexer #(.width(16), .enable("false")) multiplexer_7 (
    .in0(out_3), .in1(ram_1_data), .out(out_4), .sel(controlunit_1_memtoreg));

  assign out_6 = out_2[15:4];

  // Notes on the sheet:
  //   HaltControl
  //   contents of rom_1 (hex, n*v repeats v):
  //   0 18 228 4a8 1040 a3f6 f
  //    r type
  //    i type
endmodule

module RegisterFile (
  input  RegWrite,
  input  zeroRead2,
  input  [2:0] Read_Register1,
  input  [2:0] Read_Register2,
  input  [2:0] Write_register,
  input  [15:0] data,
  input  clock,
  input  Reset,
  output [15:0] Data1,
  output [15:0] Data2
);

  wire and_1_out, and_2_out, and_3_out, and_4_out, and_5_out, and_6_out, and_7_out, and_8_out,
       decoder_1_out0, decoder_1_out1, decoder_1_out2, decoder_1_out3, decoder_1_out4, decoder_1_out5,
       decoder_1_out6, decoder_1_out7;
  wire [15:0] multiplexer_1_out, register_1_q, register_2_q, register_3_q, register_4_q, register_5_q,
       register_6_q, register_7_q, register_8_q;

  Decoder #(.select(3), .enable("false")) decoder_1 (
    .out0(decoder_1_out0), .out1(decoder_1_out1), .out2(decoder_1_out2), .out3(decoder_1_out3),
    .out4(decoder_1_out4), .out5(decoder_1_out5), .out6(decoder_1_out6), .out7(decoder_1_out7),
    .sel(Write_register));
  and and_1 (and_1_out, decoder_1_out0, RegWrite);
  and and_2 (and_2_out, decoder_1_out1, RegWrite);
  and and_3 (and_3_out, decoder_1_out2, RegWrite);
  and and_4 (and_4_out, decoder_1_out3, RegWrite);
  and and_5 (and_5_out, decoder_1_out4, RegWrite);
  and and_6 (and_6_out, decoder_1_out5, RegWrite);
  and and_7 (and_7_out, decoder_1_out6, RegWrite);
  and and_8 (and_8_out, decoder_1_out7, RegWrite);
  Register #(.width(16)) register_1 (.D(data), .en(and_1_out), .Q(register_1_q), .clk(clock), .clr(Reset));
  Register #(.width(16)) register_2 (.D(data), .en(and_2_out), .Q(register_2_q), .clk(clock), .clr(Reset));
  Register #(.width(16)) register_3 (.D(data), .en(and_3_out), .Q(register_3_q), .clk(clock), .clr(Reset));
  Register #(.width(16)) register_4 (.D(data), .en(and_4_out), .Q(register_4_q), .clk(clock), .clr(Reset));
  Register #(.width(16)) register_5 (.D(data), .en(and_5_out), .Q(register_5_q), .clk(clock), .clr(Reset));
  Register #(.width(16)) register_6 (.D(data), .en(and_6_out), .Q(register_6_q), .clk(clock), .clr(Reset));
  Register #(.width(16)) register_7 (.D(data), .en(and_7_out), .Q(register_7_q), .clk(clock), .clr(Reset));
  Register #(.width(16)) register_8 (.D(data), .en(and_8_out), .Q(register_8_q), .clk(clock), .clr(Reset));
  Multiplexer #(.select(3), .width(16), .enable("false")) multiplexer_1 (
    .in0(register_1_q), .in1(register_2_q), .in2(register_3_q), .in3(register_4_q), .in4(register_5_q),
    .in5(register_6_q), .in6(register_7_q), .in7(register_8_q), .out(multiplexer_1_out), .sel(Read_Register1));
  Multiplexer #(.select(3), .width(16), .enable("false")) multiplexer_2 (
    .in0(register_1_q), .in1(register_2_q), .in2(register_3_q), .in3(register_4_q), .in4(register_5_q),
    .in5(register_6_q), .in6(register_7_q), .in7(register_8_q), .out(Data2), .sel(Read_Register2));
  Multiplexer #(.width(16), .enable("false")) multiplexer_3 (
    .in0(multiplexer_1_out), .in1({16{1'b0}}), .out(Data1), .sel(zeroRead2));
endmodule

module NegativeIncludeExtend (
  input  [5:0] in_1,
  output [15:0] out_2
);

  wire [15:0] bit_extender_1_out, bit_extender_2_out;

  assign bit_extender_1_out = {{10{1'b0}}, in_1};  // Bit_Extender bit_extender_1
  assign bit_extender_2_out = {{10{1'b1}}, in_1};  // Bit_Extender bit_extender_2
  Multiplexer #(.width(16), .enable("false")) multiplexer_1 (
    .in0(bit_extender_1_out), .in1(bit_extender_2_out), .out(out_2), .sel(in_1[5]));
endmodule

module NegativeIncludeExtend2 (
  input  [11:0] in_1,
  output [15:0] out_2
);

  wire [15:0] bit_extender_1_out, bit_extender_2_out;

  assign bit_extender_1_out = {{4{1'b0}}, in_1};  // Bit_Extender bit_extender_1
  assign bit_extender_2_out = {{4{1'b1}}, in_1};  // Bit_Extender bit_extender_2
  Multiplexer #(.width(16), .enable("false")) multiplexer_1 (
    .in0(bit_extender_1_out), .in1(bit_extender_2_out), .out(out_2), .sel(in_1[11]));
endmodule

module ALU (
  input  [15:0] Input_data_1,
  input  [15:0] Input_data_2,
  input  [2:0] ALUop,
  output [15:0] ALU_result,
  output branchCompare
);

  wire comparator_1_lt, comparator_2_lt, not_1_out, not_2_out;
  wire [15:0] adder_1_out, and_1_out, or_1_out;

  Adder #(.width(16)) adder_1 (.a(Input_data_1), .b(Input_data_2), .out(adder_1_out));  // open: cin, cout
  assign and_1_out = Input_data_1 & Input_data_2;  // AND_Gate and_1, 16 bits wide
  assign or_1_out = Input_data_1 | Input_data_2;  // OR_Gate or_1, 16 bits wide
  Comparator #(.width(16)) comparator_1 (.a(Input_data_1), .b(Input_data_2), .lt(comparator_1_lt));  // open: gt, eq
  Comparator #(.width(16)) comparator_2 (.a(Input_data_2), .b(Input_data_1), .lt(comparator_2_lt));  // open: gt, eq
  not not_1 (not_1_out, comparator_1_lt);
  not not_2 (not_2_out, comparator_2_lt);
  Multiplexer #(.select(2), .width(16), .enable("false")) multiplexer_1 (
    .in0(adder_1_out), .in1(and_1_out), .in2(or_1_out), .in3(Input_data_2), .out(ALU_result), .sel(ALUop[1:0]));
  Multiplexer #(.enable("false")) multiplexer_2 (.in0(not_1_out), .in1(not_2_out), .out(branchCompare), .sel(ALUop[2]));

  // Notes on the sheet:
  //   add/addi
  //   and/andi
  //   or/ori
  //   ble
  //   bne
endmodule

module ControlUnit (
  input  [2:0] R_type_input,
  input  [3:0] opcode,
  output [2:0] ALUOpcode,
  output R_type,
  output RegWrite,
  output MemWrite,
  output branch,
  output RegDst,
  output ALUsrc,
  output MemRead,
  output MemToReg,
  output jump,
  output call,
  output rtn,
  output halt,
  output zeroReg
);

  wire and_1_out, and_2_out, and_3_out, and_4_out, and_7_out, and_9_out, and_10_out, and_11_out, and_12_out,
       and_19_out, and_20_out, and_21_out, and_22_out, and_23_out, and_24_out, not_1_out, not_2_out,
       not_3_out, not_4_out, not_5_out, not_6_out, not_7_out, not_8_out, not_9_out, not_10_out, not_11_out,
       not_12_out, not_13_out, not_14_out, not_15_out, not_16_out, not_17_out, not_18_out, not_19_out,
       not_20_out, not_21_out, not_22_out, not_23_out, not_24_out, not_25_out, not_26_out, not_27_out,
       not_28_out, not_29_out, not_30_out, not_31_out, not_32_out, not_33_out, not_34_out, not_35_out,
       not_36_out, not_37_out, not_38_out, not_39_out, not_40_out, not_41_out, not_42_out, not_43_out,
       not_44_out, not_45_out, not_46_out, not_47_out, or_4_out;
  wire [2:0] multiplexer_1_out;

  not not_1 (not_1_out, opcode[0]);
  not not_2 (not_2_out, opcode[1]);
  and and_1 (and_1_out, not_1_out, not_2_out);
  not not_3 (not_3_out, opcode[1]);
  not not_4 (not_4_out, opcode[2]);
  and and_2 (and_2_out, opcode[0], not_3_out, not_4_out);
  or or_1 (RegWrite, and_1_out, and_2_out, and_3_out, and_4_out);
  not not_5 (not_5_out, opcode[2]);
  not not_6 (not_6_out, opcode[3]);
  not not_7 (not_7_out, opcode[1]);
  and and_3 (and_3_out, opcode[1], not_5_out, not_6_out);
  not not_8 (not_8_out, opcode[0]);
  not not_9 (not_9_out, opcode[3]);
  and and_4 (and_4_out, opcode[0], not_7_out, opcode[2], not_9_out);
  and and_5 (MemWrite, not_8_out, opcode[1], not_10_out, opcode[3]);
  not not_10 (not_10_out, opcode[2]);
  not not_11 (not_11_out, opcode[0]);
  and and_6 (branch, not_11_out, opcode[1], opcode[2]);
  not not_12 (not_12_out, opcode[0]);
  not not_13 (not_13_out, opcode[0]);
  not not_14 (not_14_out, opcode[2]);
  not not_15 (not_15_out, opcode[3]);
  and and_7 (and_7_out, not_12_out, not_14_out, not_15_out);
  or or_2 (RegDst, and_7_out, and_9_out);
  not not_16 (not_16_out, opcode[0]);
  not not_17 (not_17_out, opcode[1]);
  not not_18 (not_18_out, opcode[3]);
  not not_19 (not_19_out, opcode[1]);
  and and_8 (zeroReg, not_16_out, not_17_out, not_22_out, opcode[3]);
  and and_9 (and_9_out, not_13_out, not_19_out, opcode[2], not_18_out);
  not not_20 (not_20_out, opcode[2]);
  not not_21 (not_21_out, opcode[3]);
  not not_22 (not_22_out, opcode[2]);
  and and_10 (and_10_out, opcode[0], not_20_out, not_21_out);
  not not_23 (not_23_out, opcode[1]);
  not not_24 (not_24_out, opcode[1]);
  not not_25 (not_25_out, opcode[0]);
  not not_26 (not_26_out, opcode[2]);
  and and_11 (and_11_out, not_25_out, not_23_out, opcode[3], not_26_out);
  or or_3 (ALUsrc, and_10_out, and_11_out, and_12_out);
  not not_27 (not_27_out, opcode[3]);
  not not_28 (not_28_out, opcode[0]);
  and and_12 (and_12_out, not_24_out, opcode[0], not_27_out, opcode[2]);
  and and_13 (MemRead, not_28_out, opcode[2], not_29_out, opcode[3]);
  not not_29 (not_29_out, opcode[1]);
  not not_30 (not_30_out, opcode[0]);
  not not_31 (not_31_out, opcode[1]);
  and and_14 (MemToReg, not_30_out, opcode[2], not_31_out, opcode[3]);
  not not_32 (not_32_out, opcode[1]);
  and and_15 (jump, opcode[0], not_32_out, opcode[2], opcode[3]);
  not not_33 (not_33_out, opcode[2]);
  and and_16 (rtn, opcode[0], opcode[1], opcode[2], not_34_out);
  and and_17 (call, opcode[0], opcode[1], not_33_out, opcode[3]);
  not not_34 (not_34_out, opcode[3]);
  and and_18 (halt, opcode[0], opcode[1], opcode[2], opcode[3]);
  not not_35 (not_35_out, opcode[0]);
  not not_36 (not_36_out, opcode[1]);
  and and_19 (and_19_out, opcode[1], not_35_out, opcode[2]);
  not not_37 (not_37_out, opcode[2]);
  not not_38 (not_38_out, opcode[3]);
  and and_20 (and_20_out, not_37_out, not_42_out);
  and and_21 (and_21_out, not_36_out, opcode[2], not_38_out);
  or or_4 (or_4_out, and_19_out, and_21_out, and_20_out);
  not not_39 (not_39_out, opcode[0]);
  not not_40 (not_40_out, opcode[2]);
  not not_41 (not_41_out, opcode[3]);
  not not_42 (not_42_out, opcode[3]);
  and and_22 (and_22_out, not_39_out, not_40_out, not_41_out);
  not not_43 (not_43_out, opcode[2]);
  not not_44 (not_44_out, opcode[1]);
  not not_45 (not_45_out, opcode[0]);
  and and_23 (and_23_out, opcode[0], not_44_out, not_43_out, opcode[3]);
  or or_5 (R_type, and_22_out, and_22_out, and_23_out, and_24_out);
  not not_46 (not_46_out, opcode[2]);
  not not_47 (not_47_out, opcode[1]);
  and and_24 (and_24_out, not_45_out, not_47_out, not_46_out, opcode[3]);
  Multiplexer #(.width(3), .enable("false")) multiplexer_1 (
    .in0(opcode[3:1]), .in1(R_type_input), .out(multiplexer_1_out), .sel(R_type));
  Multiplexer #(.width(3), .enable("false")) multiplexer_2 (
    .in0(3'b000), .in1(multiplexer_1_out), .out(ALUOpcode), .sel(or_4_out));
endmodule
