// Logisim project HW4_pipeline_v3.circ as structural Verilog: 9 circuits, main circuit main
module main (
  input  reset,
  input  in_2
);

  wire and_1_out, and_2_out, and_3_out, clock_1_out, Control_Unit_halt, Control_Unit_regdst, not_1_out,
       not_2_out, not_3_out, or_1_out, undriven_2, undriven_3, undriven_4, undriven_5, undriven_6,
       undriven_7, undriven_8, undriven_9, undriven_15, undriven_16;
  wire [2:0] multiplexer_2_out, register_1_q, undriven;
  wire [15:0] adder_1_out, adder_2_out, ALU_alu_result, exe_mem_1_memtoreg_0, exe_mem_1_memwrite_address_2,
       exe_mem_1_memwrite_data_2, i_type_immediate_out_2, if_id_1_instruction_2, if_id_1_pc_1_2,
       if_id_1_pc_2, j_type_immediate_out_2, multiplexer_1_out, multiplexer_3_out, multiplexer_4_out,
       multiplexer_5_out, multiplexer_6_out, multiplexer_7_out, PC_q, ra_q, ram_1_data, Register_File_data1,
       Register_File_data2, rom_1_data, undriven_10, undriven_11, undriven_12, undriven_13, undriven_14;

  Clock clock_1 (.out(clock_1_out));
  and and_1 (and_1_out, not_1_out, clock_1_out);
  ID_EXE id_exe_1 ();  // open: aluOp, regWrite, memWrite, branch, aluSrc, memRead, memToReg, jump, call, rtn, halt, pc, readData1, readData2, j_type_Immediate, i_type_immediate, pc_1, aluOp_2, regWrite_2, regWrite_3, branch_2, aluSrc_2, memRead_2, memToReg_2, jump_2, call_2, rtn_2, halt_2, pc_2, ALU_input_1, read_data2, j_type_Immediate_2, j_type_Immediate_3, pc_1_2, clock, reset
  Multiplexer #(.width(16), .enable("false")) multiplexer_1 (
    .in0(multiplexer_4_out), .in1(adder_1_out), .out(multiplexer_1_out), .sel(in_2));
  Register #(.width(16)) PC (.D(multiplexer_1_out), .en(1'b1), .Q(PC_q), .clk(and_1_out), .clr(reset));
  Adder #(.width(16)) adder_1 (.a(16'h1), .b(PC_q), .out(adder_1_out));  // open: cin, cout
  ROM #(.addrWidth(16), .dataWidth(16)) rom_1 (.addr(PC_q), .data(rom_1_data), .sel(1'b1));
  if_id if_id_1 (
    .PC_1(adder_1_out), .PC(PC_q), .Instruction(rom_1_data), .PC_1_2(if_id_1_pc_1_2), .PC_2(if_id_1_pc_2),
    .Instruction_2(if_id_1_instruction_2), .Clock(and_1_out), .Reset(reset));
  not not_1 (not_1_out, Control_Unit_halt);
  ControlUnit Control_Unit (
    .R_type_input({if_id_1_instruction_2[15], if_id_1_instruction_2[5:4]}),
    .opcode(if_id_1_instruction_2[3:0]), .RegDst(Control_Unit_regdst), .halt(Control_Unit_halt));  // open: R_type, ALUOpcode, RegWrite, MemWrite, branch, ALUsrc, MemRead, MemToReg, jump, call, rtn, zeroReg
  NegativeIncludeExtend2 j_type_immediate (.in_1(if_id_1_instruction_2[15:4]), .out_2(j_type_immediate_out_2));
  not not_2 (not_2_out, Control_Unit_regdst);
  Multiplexer #(.width(3), .enable("false")) multiplexer_2 (
    .in0(if_id_1_instruction_2[8:6]), .in1(if_id_1_instruction_2[11:9]), .out(multiplexer_2_out),
    .sel(not_2_out));
  NegativeIncludeExtend i_type_immediate (
    .in_1({if_id_1_instruction_2[15], if_id_1_instruction_2[8:4]}), .out_2(i_type_immediate_out_2));
  RegisterFile Register_File (
    .RegWrite(undriven_2), .Write_register(multiplexer_2_out), .Read_Register1(if_id_1_instruction_2[14:12]),
    .data(multiplexer_7_out), .Read_Register2(if_id_1_instruction_2[11:9]), .Data1(Register_File_data1),
    .Data2(Register_File_data2), .Reset(reset), .clock(and_1_out), .zeroRead2(undriven_9));
  not not_3 (not_3_out, undriven_15);
  Multiplexer #(.width(16), .enable("false")) multiplexer_3 (
    .in0(undriven_13), .in1(undriven_10), .out(multiplexer_3_out), .sel(undriven_5));
  Multiplexer #(.width(16), .enable("false")) multiplexer_4 (
    .in0(multiplexer_6_out), .in1(ra_q), .out(multiplexer_4_out), .sel(undriven_16));
  Multiplexer #(.width(16), .enable("false")) multiplexer_5 (
    .in0(j_type_immediate_out_2), .in1(undriven_10), .out(multiplexer_5_out), .sel(not_3_out));
  ALU ALU (
    .Input_data_1(undriven_14), .Input_data_2(multiplexer_3_out), .ALUop(register_1_q),
    .ALU_result(ALU_alu_result));  // open: branchCompare
  Register #(.width(3)) register_1 (.D(undriven), .Q(register_1_q), .clk(and_1_out), .clr(reset));  // open: en
  buf and_2 (and_2_out, undriven_4);  // AND_Gate
  Adder #(.width(16)) adder_2 (.a(if_id_1_pc_2), .b(multiplexer_5_out), .out(adder_2_out));  // open: cin, cout
  or or_1 (or_1_out, undriven_15, undriven_8, and_2_out);
  EXE_MEM exe_mem_1 (
    .MemWrite_address(undriven_11), .MemWrite_data(undriven_12), .ALU_result(ALU_alu_result),
    .MemWrite_address_2(exe_mem_1_memwrite_address_2), .MemWrite_data_2(exe_mem_1_memwrite_data_2),
    .MemToReg_0(exe_mem_1_memtoreg_0), .Clock(and_1_out), .Reset(reset));  // open: MemToReg, MemToReg_2, RegWrite, RegWrite_2, MemRead, RegWrite_3, MemWrite, MemWrite_2, Halt, Halt_2
  Multiplexer #(.width(16), .enable("false")) multiplexer_6 (
    .in0(if_id_1_pc_1_2), .in1(adder_2_out), .out(multiplexer_6_out), .sel(or_1_out));
  Register #(.width(16)) ra (.D(if_id_1_pc_1_2), .Q(ra_q), .clk(and_3_out));  // open: en, clr
  and and_3 (and_3_out, undriven_8, and_1_out);
  RAM #(.addrWidth(16), .dataWidth(16), .bus("separate")) ram_1 (
    .addr(exe_mem_1_memwrite_address_2), .din(exe_mem_1_memwrite_data_2), .data(ram_1_data),
    .str(undriven_3), .clk(and_1_out), .ld(undriven_6), .clr(reset));  // open: sel
  Multiplexer #(.width(16), .enable("false")) multiplexer_7 (
    .in0(exe_mem_1_memtoreg_0), .in1(ram_1_data), .out(multiplexer_7_out), .sel(undriven_7));

  // Notes on the sheet:
  //   HaltControl
  //   Instruction file
  //   contents of rom_1 (hex, n*v repeats v):
  //   0 68 248 7b 2609 78 288 3b 2809 3d 1080 7 f
  //    r type
  //    i type
  //   mem write addr
  //   mem write data
  //   1
  //   2
  //   1
  //   ALUsrc 0
  //   jump/PC+1
  //   return by ra
  //   jump/branch
  //   PC+1
  //   jump
  //   Memory
  //   clock
endmodule

module RegisterFile (
  input  RegWrite,
  input  zeroRead2,
  input  [2:0] Read_Register1,
  input  [2:0] Read_Register2,
  input  [2:0] Write_register,
  input  [15:0] data,
  input  clock,
  input  Reset,
  output [15:0] Data1,
  output [15:0] Data2
);

  wire and_1_out, and_2_out, and_3_out, and_4_out, and_5_out, and_6_out, and_7_out, and_8_out,
       decoder_1_out0, decoder_1_out1, decoder_1_out2, decoder_1_out3, decoder_1_out4, decoder_1_out5,
       decoder_1_out6, decoder_1_out7;
  wire [15:0] multiplexer_1_out, register_1_q, register_2_q, register_3_q, register_4_q, register_5_q,
       register_6_q, register_7_q, register_8_q;

  Decoder #(.select(3), .enable("false")) decoder_1 (
    .out0(decoder_1_out0), .out1(decoder_1_out1), .out2(decoder_1_out2), .out3(decoder_1_out3),
    .out4(decoder_1_out4), .out5(decoder_1_out5), .out6(decoder_1_out6), .out7(decoder_1_out7),
    .sel(Write_register));
  and and_1 (and_1_out, decoder_1_out0, RegWrite);
  and and_2 (and_2_out, decoder_1_out1, RegWrite);
  and and_3 (and_3_out, decoder_1_out2, RegWrite);
  and and_4 (and_4_out, decoder_1_out3, RegWrite);
  and and_5 (and_5_out, decoder_1_out4, RegWrite);
  and and_6 (and_6_out, decoder_1_out5, RegWrite);
  and and_7 (and_7_out, decoder_1_out6, RegWrite);
  and and_8 (and_8_out, decoder_1_out7, RegWrite);
  Register #(.width(16)) register_1 (.D(data), .en(and_1_out), .Q(register_1_q), .clk(clock), .clr(Reset));
  Register #(.width(16)) register_2 (.D(data), .en(and_2_out), .Q(register_2_q), .clk(clock), .clr(Reset));
  Register #(.width(16)) register_3 (.D(data), .en(and_3_out), .Q(register_3_q), .clk(clock), .clr(Reset));
  Register #(.width(16)) register_4 (.D(data), .en(and_4_out), .Q(register_4_q), .clk(clock), .clr(Reset));
  Register #(.width(16)) register_5 (.D(data), .en(and_5_out), .Q(register_5_q), .clk(clock), .clr(Reset));
  Register #(.width(16)) register_6 (.D(data), .en(and_6_out), .Q(register_6_q), .clk(clock), .clr(Reset));
  Register #(.width(16)) register_7 (.D(data), .en(and_7_out), .Q(register_7_q), .clk(clock), .clr(Reset));
  Register #(.width(16)) register_8 (.D(data), .en(and_8_out), .Q(register_8_q), .clk(clock), .clr(Reset));
  Multiplexer #(.select(3), .width(16), .enable("false")) multiplexer_1 (
    .in0(register_1_q), .in1(register_2_q), .in2(register_3_q), .in3(register_4_q), .in4(register_5_q),
    .in5(register_6_q), .in6(register_7_q), .in7(register_8_q), .out(multiplexer_1_out), .sel(Read_Register1));
  Multiplexer #(.select(3), .width(16), .enable("false")) multiplexer_2 (
    .in0(register_1_q), .in1(register_2_q), .in2(register_3_q), .in3(register_4_q), .in4(register_5_q),
    .in5(register_6_q), .in6(register_7_q), .in7(register_8_q), .out(Data2), .sel(Read_Register2));
  Multiplexer #(.width(16), .enable("false")) multiplexer_3 (
    .in0(multiplexer_1_out), .in1({16{1'b0}}), .out(Data1), .sel(zeroRead2));
endmodule

module NegativeIncludeExtend (
  input  [5:0] in_1,
  output [15:0] out_2
);

  wire [15:0] bit_extender_1_out, bit_extender_2_out;

  assign bit_extender_1_out = {{10{1'b0}}, in_1};  // Bit_Extender bit_extender_1
  assign bit_extender_2_out = {{10{1'b1}}, in_1};  // Bit_Extender bit_extender_2
  Multiplexer #(.width(16), .enable("false")) multiplexer_1 (
    .in0(bit_extender_1_out), .in1(bit_extender_2_out), .out(out_2), .sel(in_1[5]));
endmodule

module NegativeIncludeExtend2 (
  input  [11:0] in_1,
  output [15:0] out_2
);

  wire [15:0] bit_extender_1_out, bit_extender_2_out;

  assign bit_extender_1_out = {{4{1'b0}}, in_1};  // Bit_Extender bit_extender_1
  assign bit_extender_2_out = {{4{1'b1}}, in_1};  // Bit_Extender bit_extender_2
  Multiplexer #(.width(16), .enable("false")) multiplexer_1 (
    .in0(bit_extender_1_out), .in1(bit_extender_2_out), .out(out_2), .sel(in_1[11]));
endmodule

module ALU (
  input  [15:0] Input_data_1,
  input  [15:0] Input_data_2,
  input  [2:0] ALUop,
  output [15:0] ALU_result,
  output branchCompare
);

  wire comparator_1_lt, comparator_2_lt, not_1_out, not_2_out;
  wire [15:0] adder_1_out, and_1_out, or_1_out;

  Adder #(.width(16)) adder_1 (.a(Input_data_1), .b(Input_data_2), .out(adder_1_out));  // open: cin, cout
  assign and_1_out = Input_data_1 & Input_data_2;  // AND_Gate and_1, 16 bits wide
  assign or_1_out = Input_data_1 | Input_data_2;  // OR_Gate or_1, 16 bits wide
  Comparator #(.width(16)) comparator_1 (.a(Input_data_1), .b(Input_data_2), .lt(comparator_1_lt));  // open: gt, eq
  Comparator #(.width(16)) comparator_2 (.a(Input_data_2), .b(Input_data_1), .lt(comparator_2_lt));  // open: gt, eq
  not not_1 (not_1_out, comparator_1_lt);
  not not_2 (not_2_out, comparator_2_lt);
  Multiplexer #(.select(2), .width(16), .enable("false")) multiplexer_1 (
    .in0(adder_1_out), .in1(and_1_out), .in2(or_1_out), .in3(Input_data_2), .out(ALU_result), .sel(ALUop[1:0]));
  Multiplexer #(.enable("false")) multiplexer_2 (.in0(not_1_out), .in1(not_2_out), .out(branchCompare), .sel(ALUop[2]));

  // Notes on the sheet:
  //   add/addi
  //   and/andi
  //   or/ori
  //   ble
  //   bne
endmodule

module ControlUnit (
  input  [2:0] R_type_input,
  input  [3:0] opcode,
  output [2:0] ALUOpcode,
  output R_type,
  output RegWrite,
  output MemWrite,
  output branch,
  output RegDst,
  output ALUsrc,
  output MemRead,
  output MemToReg,
  output jump,
  output call,
  output rtn,
  output halt,
  output zeroReg
);

  wire and_1_out, and_2_out, and_3_out, and_5_out, and_7_out, and_9_out, and_10_out, and_11_out, and_13_out,
       and_19_out, and_20_out, and_21_out, and_22_out, and_23_out, and_24_out, not_1_out, not_2_out,
       not_3_out, not_4_out, not_5_out, not_6_out, not_7_out, not_8_out, not_9_out, not_10_out, not_11_out,
       not_12_out, not_13_out, not_14_out, not_15_out, not_16_out, not_17_out, not_18_out, not_19_out,
       not_20_out, not_21_out, not_22_out, not_23_out, not_24_out, not_25_out, not_26_out, not_27_out,
       not_28_out, not_29_out, not_30_out, not_31_out, not_32_out, not_33_out, not_34_out, not_35_out,
       not_36_out, not_37_out, not_38_out, not_39_out, not_40_out, not_41_out, not_42_out, not_43_out,
       not_44_out, not_45_out, not_46_out, not_47_out, or_4_out, or_5_out;
  wire [2:0] multiplexer_1_out;

  not not_1 (not_1_out, opcode[1]);
  not not_2 (not_2_out, opcode[0]);
  and and_1 (and_1_out, not_2_out, not_1_out);
  not not_3 (not_3_out, opcode[2]);
  not not_4 (not_4_out, opcode[1]);
  and and_2 (and_2_out, opcode[0], not_4_out, not_3_out);
  or or_1 (RegWrite, and_1_out, and_2_out, and_3_out, and_5_out);
  not not_5 (not_5_out, opcode[1]);
  not not_6 (not_6_out, opcode[2]);
  not not_7 (not_7_out, opcode[3]);
  and and_3 (and_3_out, opcode[1], not_6_out, not_7_out);
  not not_8 (not_8_out, opcode[0]);
  not not_9 (not_9_out, opcode[3]);
  and and_4 (MemWrite, not_8_out, opcode[1], not_11_out, opcode[3]);
  and and_5 (and_5_out, opcode[0], not_5_out, opcode[2], not_9_out);
  not not_10 (not_10_out, opcode[0]);
  not not_11 (not_11_out, opcode[2]);
  and and_6 (branch, not_10_out, opcode[1], opcode[2]);
  not not_12 (not_12_out, opcode[0]);
  not not_13 (not_13_out, opcode[2]);
  not not_14 (not_14_out, opcode[0]);
  not not_15 (not_15_out, opcode[3]);
  and and_7 (and_7_out, not_14_out, not_13_out, not_15_out);
  or or_2 (RegDst, and_7_out, and_9_out);
  not not_16 (not_16_out, opcode[0]);
  not not_17 (not_17_out, opcode[3]);
  not not_18 (not_18_out, opcode[1]);
  not not_19 (not_19_out, opcode[1]);
  and and_8 (zeroReg, not_16_out, not_18_out, not_20_out, opcode[3]);
  and and_9 (and_9_out, not_12_out, not_19_out, opcode[2], not_17_out);
  not not_20 (not_20_out, opcode[2]);
  not not_21 (not_21_out, opcode[3]);
  not not_22 (not_22_out, opcode[2]);
  and and_10 (and_10_out, opcode[0], not_22_out, not_21_out);
  not not_23 (not_23_out, opcode[1]);
  not not_24 (not_24_out, opcode[2]);
  not not_25 (not_25_out, opcode[0]);
  not not_26 (not_26_out, opcode[1]);
  and and_11 (and_11_out, not_25_out, not_23_out, opcode[3], not_24_out);
  or or_3 (ALUsrc, and_10_out, and_11_out, and_13_out);
  not not_27 (not_27_out, opcode[0]);
  not not_28 (not_28_out, opcode[3]);
  and and_12 (MemRead, not_27_out, opcode[2], not_29_out, opcode[3]);
  and and_13 (and_13_out, not_26_out, opcode[0], not_28_out, opcode[2]);
  not not_29 (not_29_out, opcode[1]);
  not not_30 (not_30_out, opcode[1]);
  not not_31 (not_31_out, opcode[0]);
  and and_14 (MemToReg, not_31_out, opcode[2], not_30_out, opcode[3]);
  not not_32 (not_32_out, opcode[1]);
  and and_15 (jump, opcode[0], not_32_out, opcode[2], opcode[3]);
  not not_33 (not_33_out, opcode[2]);
  and and_16 (rtn, opcode[0], opcode[1], opcode[2], not_34_out);
  and and_17 (call, opcode[0], opcode[1], not_33_out, opcode[3]);
  not not_34 (not_34_out, opcode[3]);
  and and_18 (halt, opcode[0], opcode[1], opcode[2], opcode[3]);
  not not_35 (not_35_out, opcode[0]);
  not not_36 (not_36_out, opcode[1]);
  and and_19 (and_19_out, opcode[1], not_35_out, opcode[2]);
  or or_4 (or_4_out, rtn, call, jump, branch);
  not not_37 (not_37_out, opcode[3]);
  not not_38 (not_38_out, opcode[2]);
  and and_20 (and_20_out, not_38_out, not_42_out);
  and and_21 (and_21_out, not_36_out, opcode[2], not_37_out);
  or or_5 (or_5_out, and_19_out, and_21_out, and_20_out);
  not not_39 (not_39_out, opcode[0]);
  not not_40 (not_40_out, opcode[3]);
  not not_41 (not_41_out, opcode[2]);
  not not_42 (not_42_out, opcode[3]);
  and and_22 (and_22_out, not_39_out, not_41_out, not_40_out);
  not not_43 (not_43_out, opcode[2]);
  not not_44 (not_44_out, opcode[1]);
  not not_45 (not_45_out, opcode[0]);
  and and_23 (and_23_out, opcode[0], not_44_out, not_43_out, opcode[3]);
  or or_6 (R_type, and_22_out, and_22_out, and_23_out, and_24_out);
  not not_46 (not_46_out, opcode[2]);
  not not_47 (not_47_out, opcode[1]);
  and and_24 (and_24_out, not_45_out, not_47_out, not_46_out, opcode[3]);
  Multiplexer #(.width(3), .enable("false")) multiplexer_1 (
    .in0(opcode[3:1]), .in1(R_type_input), .out(multiplexer_1_out), .sel(R_type));
  Multiplexer #(.width(3), .enable("false")) multiplexer_2 (
    .in0(3'b000), .in1(multiplexer_1_out), .out(ALUOpcode), .sel(or_5_out));
endmodule

module if_id (
  input  [15:0] PC_1,
  input  [15:0] PC,
  input  [15:0] Instruction,
  input  Clock,
  input  Reset,
  output [15:0] PC_1_2,
  output [15:0] PC_2,
  output [15:0] Instruction_2
);

  Register #(.width(16)) register_1 (.D(PC_1), .Q(PC_1_2), .clk(Clock), .clr(Reset));  // open: en
  Register #(.width(16)) register_2 (.D(PC), .Q(PC_2), .clk(Clock), .clr(Reset));  // open: en
  Register #(.width(16)) register_3 (.D(Instruction), .Q(Instruction_2), .clk(Clock), .clr(Reset));  // open: en
endmodule

module EXE_MEM (
  input  Halt,
  input  MemToReg,
  input  RegWrite,
  input  MemWrite,
  input  MemRead,
  input  [15:0] MemWrite_address,
  input  [15:0] MemWrite_data,
  input  [15:0] ALU_result,
  input  Clock,
  input  Reset,
  output Halt_2,
  output MemToReg_2,
  output RegWrite_2,
  output MemWrite_2,
  output RegWrite_3,
  output [15:0] MemWrite_address_2,
  output [15:0] MemWrite_data_2,
  output [15:0] MemToReg_0
);

  Register #(.width(1)) register_1 (.D(Halt), .Q(Halt_2), .clk(Clock), .clr(Reset));  // open: en
  Register #(.width(1)) register_2 (.D(MemToReg), .Q(MemToReg_2), .clk(Clock), .clr(Reset));  // open: en
  Register #(.width(1)) register_3 (.D(RegWrite), .Q(RegWrite_2), .clk(Clock), .clr(Reset));  // open: en
  Register #(.width(1)) register_4 (.D(MemWrite), .Q(MemWrite_2), .clk(Clock), .clr(Reset));  // open: en
  Register #(.width(1)) register_5 (.D(MemRead), .Q(RegWrite_3), .clk(Clock), .clr(Reset));  // open: en
  Register #(.width(16)) register_6 (
    .D(MemWrite_address), .Q(MemWrite_address_2), .clk(Clock), .clr(Reset));  // open: en
  Register #(.width(16)) register_7 (.D(MemWrite_data), .Q(MemWrite_data_2), .clk(Clock), .clr(Reset));  // open: en
  Register #(.width(16)) register_8 (.D(ALU_result), .Q(MemToReg_0), .clk(Clock), .clr(Reset));  // open: en
endmodule

module ID_EXE (
  input  [2:0] aluOp,
  input  regWrite,
  input  memWrite,
  input  branch,
  input  aluSrc,
  input  memRead,
  input  memToReg,
  input  jump,
  input  call,
  input  rtn,
  input  halt,
  input  [15:0] pc,
  input  [15:0] readData1,
  input  [15:0] readData2,
  input  [15:0] j_type_Immediate,
  input  [15:0] i_type_immediate,
  input  [15:0] pc_1,
  input  clock,
  input  reset,
  output [2:0] aluOp_2,
  output regWrite_2,
  output regWrite_3,
  output branch_2,
  output aluSrc_2,
  output memRead_2,
  output memToReg_2,
  output jump_2,
  output call_2,
  output rtn_2,
  output halt_2,
  output [15:0] pc_2,
  output [15:0] ALU_input_1,
  output [15:0] read_data2,
  output [15:0] j_type_Immediate_2,
  output [15:0] j_type_Immediate_3,
  output [15:0] pc_1_2
);

  Register #(.width(3)) register_1 (.D(aluOp), .Q(aluOp_2), .clk(clock), .clr(reset));  // open: en
  Register #(.width(1)) register_2 (.D(regWrite), .Q(regWrite_2), .clk(clock), .clr(reset));  // open: en
  Register #(.width(1)) register_3 (.D(memWrite), .Q(regWrite_3), .clk(clock), .clr(reset));  // open: en
  Register #(.width(1)) register_4 (.D(branch), .Q(branch_2), .clk(clock), .clr(reset));  // open: en
  Register #(.width(1)) register_5 (.D(aluSrc), .Q(aluSrc_2), .clk(clock), .clr(reset));  // open: en
  Register #(.width(1)) register_6 (.D(memRead), .Q(memRead_2), .clk(clock), .clr(reset));  // open: en
  Register #(.width(1)) register_7 (.D(memToReg), .Q(memToReg_2), .clk(clock), .clr(reset));  // open: en
  Register #(.width(1)) register_8 (.D(jump), .Q(jump_2), .clk(clock), .clr(reset));  // open: en
  Register #(.width(1)) register_9 (.D(call), .Q(call_2), .clk(clock), .clr(reset));  // open: en
  Register #(.width(1)) register_10 (.D(rtn), .Q(rtn_2), .clk(clock), .clr(reset));  // open: en
  Register #(.width(1)) register_11 (.D(halt), .Q(halt_2), .clk(clock), .clr(reset));  // open: en
  Register #(.width(16)) register_12 (.D(pc), .Q(pc_2), .clk(clock), .clr(reset));  // open: en
  Register #(.width(16)) register_13 (.D(readData1), .Q(ALU_input_1), .clk(clock), .clr(reset));  // open: en
  Register #(.width(16)) register_14 (.D(readData2), .Q(read_data2), .clk(clock), .clr(reset));  // open: en
  Register #(.width(16)) register_15 (
    .D(j_type_Immediate), .Q(j_type_Immediate_2), .clk(clock), .clr(reset));  // open: en
  Register #(.width(16)) register_16 (
    .D(i_type_immediate), .Q(j_type_Immediate_3), .clk(clock), .clr(reset));  // open: en
  Register #(.width(16)) register_17 (.D(pc_1), .Q(pc_1_2), .clk(clock), .clr(reset));  // open: en
endmodule
