// Logisim project id_ex.circ as structural Verilog: 2 circuits, main circuit main
module main (
  input  [2:0] aluOp,
  input  regWrite,
  input  memWrite,
  input  branch,
  input  aluSrc,
  input  memRead,
  input  memToReg,
  input  jump,
  input  call,
  input  rtn,
  input  [15:0] pc_4,
  input  [15:0] readData1,
  input  [15:0] readData2,
  input  [15:0] j_type_Immediate,
  input  [15:0] i_type_immediate,
  input  clock,
  input  reset,
  output [2:0] aluOp_2,
  output regWrite_2,
  output regWrite_3,
  output branch_2,
  output aluSrc_2,
  output memRead_2,
  output memToReg_2,
  output jump_2,
  output call_2,
  output rtn_2,
  output [15:0] pc_4_2,
  output [15:0] ALU_input_1,
  output [15:0] read_data2,
  output [15:0] j_type_Immediate_2,
  output [15:0] j_type_Immediate_3
);

  Register #(.width(3)) register_1 (.D(aluOp), .Q(aluOp_2), .clk(clock), .clr(reset));  // open: en
  Register #(.width(1)) register_2 (.D(regWrite), .Q(regWrite_2), .clk(clock), .clr(reset));  // open: en
  Register #(.width(1)) register_3 (.D(memWrite), .Q(regWrite_3), .clk(clock), .clr(reset));  // open: en
  Register #(.width(1)) register_4 (.D(branch), .Q(branch_2), .clk(clock), .clr(reset));  // open: en
  Register #(.width(1)) register_5 (.D(aluSrc), .Q(aluSrc_2), .clk(clock), .clr(reset));  // open: en
  Register #(.width(1)) register_6 (.D(memRead), .Q(memRead_2), .clk(clock), .clr(reset));  // open: en
  Register #(.width(1)) register_7 (.D(memToReg), .Q(memToReg_2), .clk(clock), .clr(reset));  // open: en
  Register #(.width(1)) register_8 (.D(jump), .Q(jump_2), .clk(clock), .clr(reset));  // open: en
  Register #(.width(1)) register_9 (.D(call), .Q(call_2), .clk(clock), .clr(reset));  // open: en
  Register #(.width(1)) register_10 (.D(rtn), .Q(rtn_2), .clk(clock), .clr(reset));  // open: en
  Register #(.width(16)) register_11 (.D(pc_4), .Q(pc_4_2), .clk(clock), .clr(reset));  // open: en
  Register #(.width(16)) register_12 (.D(readData1), .Q(ALU_input_1), .clk(clock), .clr(reset));  // open: en
  Register #(.width(16)) register_13 (.D(readData2), .Q(read_data2), .clk(clock), .clr(reset));  // open: en
  Register #(.width(16)) register_14 (
    .D(j_type_Immediate), .Q(j_type_Immediate_2), .clk(clock), .clr(reset));  // open: en
  Register #(.width(16)) register_15 (
    .D(i_type_immediate), .Q(j_type_Immediate_3), .clk(clock), .clr(reset));  // open: en
endmodule

module id_ex (
  input  in_1
);
endmodule
